# Fritzing sketch Arduino_Shield_Attiny_Programmer (saved by Fritzing 0.9.2b)
circuit board: 3.18983cm x 5.2648cm
breadboards: 1

parts:
  U1 = attiny85 [package=dip]
  C1 = Electrolytic Capacitor [capacitance=1µF package="200 mil [THT, electrolytic]"]
  Part1 = Arduino Uno (Rev3)
  U2 = atmega328 [package=dip]  # not connected

nets:
  N1: U1.Pin_1, Part1.D10_PWM/SS
  GND: U1.Pin_4, C1.-, Part1.GND
  N2: U1.Pin_5, Part1.D11_PWM/MOSI
  N3: U1.Pin_6, Part1.D12/MISO
  N4: U1.Pin_7, Part1.D13/SCK
  N5: U1.Pin_8, Part1.5V
  N6: C1.+, Part1.RESET

notes:
  Attiny
  Nickified
  ISP
  45/85
